# Fritzing sketch arduino-lcd-display (saved by Fritzing 0.8.5b)

parts:
  Composants1 = DeuLigne 1.1 - The Snootlab's LCD shield for Arduino
  Composants2 = Arduino Uno (Rev3)

nets:
  N1: Composants1.D8, Composants2.D8
  N2: Composants1.D9, Composants2.D9_PWM
  N3: Composants1.D10_SS, Composants2.D10_PWM/SS
  N4: Composants1.D4, Composants2.D4
  N5: Composants1.D5, Composants2.D5_PWM
  N6: Composants1.D6, Composants2.D6_PWM
  N7: Composants1.D7, Composants2.D7
  N8: Composants1.RESET, Composants2.A5/SCL
  +5V: Composants1.+5V, Composants2.5V
  GND: Composants1.GND, Composants2.GND
  N9: Composants1.A0, Composants2.A0
