# Fritzing sketch communication_i2c (saved by Fritzing 0.8.5b)

parts:
  Composants1 = Arduino Uno (Rev3)
  Raspberry_Pi_B_rev1 = Raspberry Pi B rev2

nets:
  N1: Composants1.A4/SDA, Raspberry_Pi_B_rev1.GPIO_2
  N2: Composants1.A5/SCL, Raspberry_Pi_B_rev1.GPIO_3
  GND: Composants1.GND, Raspberry_Pi_B_rev1.GND
